# Fritzing sketch BinkyDCC (saved by Fritzing 0.9.3b)
circuit board: 3.59037cm x 2.4638cm
breadboards: 1

parts:
  Q1 = NPN-Transistor [part_number=BC547 package="TO92 [THT]"]
  R1 = Resistor [tolerance=±5% resistance=1k package=THT]
  R2 = Resistor [tolerance=±5% resistance=1k package=THT]
  R3 = Resistor [tolerance=±5% resistance=10k package=THT]
  J1 = double row female pin header, 8 pins [form="♀ (female)"]
  J2 = female pin header, 4 pins [form="♀ (female)"]
  U1 = ATTINY13 [package=dip]  # not connected

nets:
  GND: Q1.E, R3.Pin_1, J1.pin8, J2.pin2
  N1: Q1.B, R2.Pin_1
  N2: Q1.C, R1.Pin_1, J1.pin2
  5V: R1.Pin_0, J1.pin3, J1.pin4, J1.pin7, J2.pin1
  N3: R2.Pin_0, J1.pin1, J2.pin3
  N4: R3.Pin_0, J1.pin5, J1.pin6, J2.pin4

notes:
  1=5V, 2=GND, 3=PWM, 4=CurrentFeedback
  ArduinoBooster
